# Fritzing sketch ESP01_LightMeter (saved by Fritzing 0.9.2b)
breadboards: 1

parts:
  U1 = ESP8266 WiFi Module [part_number=ESP8266]
  P1 = S1133 Si Photodiode [part_number=PT333-3C package="8mm Ceramic [THT]"]
  C1 = Electrolytic Capacitor [capacitance=0.47mF package="100 mil [THT, electrolytic]"]
  R1 = Resistor [tolerance=±5% resistance=220 package=THT]
  Part1 = FTDI Basic Programmer
  S1 = SWITCH-MOMENTARY-2 [package=tactile-switch-1101ne]
  R2 = Resistor [tolerance=±5% resistance=10k package=THT]
  U2 = Voltage Regulator LM1117 [part_number=1117 package=sot223]
  R3 = Resistor [tolerance=±5% resistance=10k package=THT]

nets:
  N1: U1.RXD, Part1.TXO
  3.3V: U1.VCC, U1.CH_PD, C1.+, R2.Pin_1, U2.OUT, R3.Pin_1
  N2: U1.GPIO_16, R3.Pin_0
  N3: U1.GPIO_2, R1.Pin_1
  GND: U1.GND, P1.anode, Part1.GND, S1.1, U2.ADJ
  N4: U1.TXD, Part1.RXI
  N5: P1.cathode, C1.-, R1.Pin_0
  N6: Part1.POWER, U2.IN
  N7: S1.2, R2.Pin_0

custom parts:
  ESP8266 WiFi Module: Generic WiFi Module based on the ESP8266 with onboard PCB antenna and UART communications
